# Fritzing sketch Fritzing (saved by Fritzing 0.9.5d)

parts:
  A1 = DORHEA ESP32 GPIO breakout board 30pin
  M1 = PH meter with sensor in breadboard [package=THT]
  A2 = tds-sensor-meter-v1.0_1
  U1 = Turbidity Sensor Probe [package=THT]
  DS1 = DS18B20 1-Wire Temperature Sensor Probe
  CPU1 = NodeMCU WROOM ESP 32  # not connected

nets:
  N1: A1.Pin_5, M1.pin1
  N2: A1.Pin_6, A2.pin1
  N3: A1.Pin_7, U1.VCC
  N4: A1.Pin_27, A1.Pin_56, A1.Pin_57, A1.Pin_58, A1.Pin_67, A1.Pin_85, M1.pin3, A2.pin3, U1.pin2, DS1.GND
  N5: A1.Pin_59, U1.pin1
  N6: A1.Pin_61, A1.Pin_62, A1.Pin_65, M1.pin2, A2.pin2, DS1.VDD
  N7: A1.Pin_76, A1.Pin_123, DS1.DQ

custom parts:
  DORHEA ESP32 GPIO breakout board 30pin: ESP32 shield 30P expansion board, supports two power supply : DC 6.5-16v and USB 5.V
  PH meter with sensor in breadboard: DFrobot PH meter (SKU SEN0161)
  : TDS Meter V1.0 Development Board Water Meter Filter Measuring Water Sensor Module.
  Turbidity Sensor Probe: Turbidity sensor probe to the DFRobot measure module.
  NodeMCU WROOM ESP 32: 30 pol Development Kit
